# Fritzing sketch schematic (saved by Fritzing 1.0.1rc)
breadboards: 1

parts:
  R1 = Resistor [tolerance=±5% power=0.25W resistance=220 package=THT]
  R2 = Resistor [tolerance=±5% power=0.25W resistance=220 package=THT]
  R3 = Resistor [tolerance=±5% power=0.25W resistance=220 package=THT]
  J1 = Piezo Speaker
  U1 = Arduino Mega 2560 (Rev3)
  LED1 = LED - 5mm [color="Green (555nm)" current=0.030A package="5 mm [THT]"]
  LED2 = LED - 5mm [color="Yellow (595nm)" current=0.030A package="5 mm [THT]"]
  LED3 = LED - 5mm [color="Red (633nm)" current=0.030A package="5 mm [THT]"]
  S1 = Pushbutton [package="[THT]"]
  R4 = Resistor [tolerance=±5% power=0.25W resistance=10k package=THT]

nets:
  N1: R1.Pin_0, LED1.anode
  N2: R1.Pin_1, U1.D10_PWM
  N3: R2.Pin_0, LED2.anode
  N4: R2.Pin_1, U1.D11_PWM
  N5: R3.Pin_0, LED3.anode
  N6: R3.Pin_1, U1.D12_PWM
  GND: J1.pin1, U1.GND, LED1.cathode, LED2.cathode, LED3.cathode, R4.Pin_1
  N7: J1.pin2, U1.D6_PWM
  N8: U1.5V, S1.Pin_1, S1.Pin_2
  N9: U1.D3_PWM, S1.Pin_3, S1.Pin_4, R4.Pin_0

// code stored in the sketch: traffic_light.ino
// Andre Reyes, Conor Duston and Harrington Idahosa modified for Lab 1 - Traffic Light Controller of EECE.4520/5520
// 10/9/2023
//
// original source:-
//timer interrupts
//by Amanda Ghassaei
//June 2012
//https://www.instructables.com/id/Arduino-Timer-Interrupts/

/*
 * This program is free software; you can redistribute it and/or modify
 * it under the terms of the GNU General Public License as published by
 * the Free Software Foundation; either version 3 of the License, or
 * (at your option) any later version.
 *
*/

//timer setup for timer0, timer1, and timer2.
//For arduino uno or any board with ATMEL 328/168.. diecimila, duemilanove, lilypad, nano, mini...

//this code will enable one arduino timer interrupt
//timer1 will interrupt at 2Hz

//Definitions for timer change points
//Time is given in seconds
#define BUZZER_ACTIVATION_TIME 3
#define FLASHING_START_TIME 3

#define red_ledpin 10
#define yellow_ledpin 11
#define green_ledpin 12

#define buzzer_pin 6

#define buttonInterruptPin 3


//State enumeration
enum light_states {
  reset,
  red,
  yellow,
  green
};

//storage variables
boolean toggle1 = 0;
volatile bool buttonPressed = false;

volatile unsigned int seconds_left = 0;

volatile light_states this_state = reset;

volatile byte current_light = red_ledpin;
volatile byte light_state = HIGH;

void setup(){
  //Serial.begin(9600);
  //set pins as outputs
  pinMode(red_ledpin, OUTPUT);
  pinMode(yellow_ledpin, OUTPUT);
  pinMode(green_ledpin, OUTPUT);

  pinMode(buzzer_pin, OUTPUT);

  pinMode(buttonInterruptPin, INPUT);
  attachInterrupt(digitalPinToInterrupt(buttonInterruptPin), solidState, RISING); //initiates button interrupt (pin to watch for interrupt, function to execute on interrupt, when interrupt should trigger[i.e. rising, falling, high, low])

  cli();//stop interrupts

  //set timer1 interrupt at 1Hz
  TCCR1A = 0;// set entire TCCR1A register to 0
  TCCR1B = 0;// same for TCCR1B
  TCNT1  = 0;//initialize counter value to 0
  // set compare match register for 2hz increments
  OCR1A = 7812;// = (16*10^6) / (2*1024) - 1 (must be <65536)
  // turn on CTC mode
  TCCR1B |= (1 << WGM12);
  // Set CS12 and CS10 bits for 1024 prescaler
  TCCR1B |= (1 << CS12) | (1 << CS10);  
  // enable timer compare interrupt
  TIMSK1 |= (1 << OCIE1A);

  sei();//allow interrupts

}//end setup

// Timer1's interrupt service routing (ISR)
// The code in ISR will be executed every time timer1 interrupt occurs
// That is, the code will be called once every half second
// TODO
//   you need to set a flag to trigger an evaluation of the conditions
//   in your buttonPressed machine, then potentially transit to next buttonPressed
//
ISR(TIMER1_COMPA_vect){//timer1 interrupt 2Hz, downsteps to 1hz
//generates pulse wave of frequency 2Hz/2 = 1Hz (based on timer interopts being raised))
  
  if (toggle1){
    //Serial.println("Toggle reset low");
    toggle1 = 0;
    
    if (this_state == reset) {
      //Serial.println("State is reset, doing nothing");
      return;
    }

    if(seconds_left <= FLASHING_START_TIME && (this_state == red || this_state == green)) {
      //Serial.println("Flash low");
      digitalWrite(current_light, HIGH);
    }
  }
  else{
    toggle1 = 1;
    
    //Serial.println("Toggle reset HIGH");

    //Reset state. only change on button interupt
    if (this_state == reset) {
      //Serial.println("Changing light state...");
      
      light_state ^= 1; // XOR'd to switch value between 0 and 1
      digitalWrite(red_ledpin, light_state);
      return;
    } 
    
    // Change state
    if (seconds_left == 0) {
      deactivate_buzzer();
      set_next_state();
    }
    //Evaluate if flashing light should occur
    if (seconds_left <= FLASHING_START_TIME && (this_state == red || this_state == green)) {
      //Serial.println("Flash Low");
      digitalWrite(current_light, LOW);
    }
    //Evaluate if buzzer should be activated
    if (seconds_left == BUZZER_ACTIVATION_TIME) {
      activate_buzzer();
    } 

    seconds_left--;
  }
}



void loop(){
  // Empty. 
  // Required by Arduino IDE, entire program controlled by Timer/button interrupts
}

void solidState(){
    if ( buttonPressed == false) {
        Serial.println("Button Pressed once");
        buttonPressed = true;
        set_next_state();
    }
}

//Set function to only output to RED LED
void set_red() {
  digitalWrite(red_ledpin, HIGH);
  digitalWrite(yellow_ledpin, LOW);
  digitalWrite(green_ledpin, LOW);
  current_light = red_ledpin;
}

void set_yellow() {
  digitalWrite(red_ledpin, LOW);
  digitalWrite(yellow_ledpin, HIGH);
  digitalWrite(green_ledpin, LOW);
  current_light = yellow_ledpin;
}

void set_green() {
  digitalWrite(red_ledpin, LOW);
  digitalWrite(yellow_ledpin, LOW);
  digitalWrite(green_ledpin, HIGH);
  current_light = green_ledpin;
}

void turn_all_off() {
  digitalWrite(red_ledpin, LOW);
  digitalWrite(yellow_ledpin, LOW);
  digitalWrite(green_ledpin, LOW);
  deactivate_buzzer();
}

void red_light() {
  set_red();
  seconds_left = 24;
}

void yellow_light() {
 set_yellow();
 seconds_left = 3;
}

void green_light() {
  set_green();
  seconds_left = 20;
}

void activate_buzzer() {
  digitalWrite(buzzer_pin, HIGH);
}

void deactivate_buzzer() {
  digitalWrite(buzzer_pin, LOW);
}

void set_next_state() {
  if (this_state == reset || this_state == yellow) {
    
    red_light();
    this_state = red;
  
  } else if (this_state == green) {

    yellow_light();
    this_state = yellow;

  } else if (this_state == red) {
    
    green_light();
    this_state = green;
  
  } else {
    //ERROR STATE, should never occur
  }
}
