# Fritzing sketch lab2-schematic (saved by Fritzing 1.0.1rc)
breadboards: 1

parts:
  U1 = Arduino Mega 2560 (Rev3)
  U2 = Adafruit Analog 2-Axis Joystick [part_number="Adafruit #512"]
  J1 = Piezo Speaker
  U3 = InvenSense MPU6050

nets:
  N1: U1.A0, U2.YOUT
  N2: U1.A1, U2.XOUT
  N3: U1.D21/SCL, U1.SCL, U3.SCL
  N4: U1.D20/SDA, U1.SDA, U3.SDA
  GND: U1.GND, U2.GND, J1.pin2, U3.GND
  5V: U1.5V, U2.VCC
  N5: U1.D4_PWM, J1.pin1
  5V_2: U3.VCC

custom parts:
  Adafruit Analog 2-Axis Joystick: This mini-kit makes it easy to mount a PSP/Xbox-like thumb joystick to your project. The thumbstick is an analog joystick - more accurate and sensitive than just 'directional' joysticks - with a 'press in to select' button. Since it's analog, you'll need two analog reading pins on your microcontroller to determine X and Y. Having an extra digital input will let you read the switch. The pack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
