# Fritzing sketch lab3-schematic (saved by Fritzing 1.0.1rc)
breadboards: 1

parts:
  Part1 = Arduino Mega 2560 (Rev3)
  M1 = DC Motor [voltage_(max)=6V voltage_(min)=3V]
  Part2 = Adafruit DS1307 RTC Breakout [part_number="Adafruit #264"]
  MIC = KY-037 Sound Sensor Module [package="Breakout board"]
  LCD1 = LCD screen
  R2 = Resistor [tolerance=±5% power=0.25W resistance=220 package=THT]
  Power_supply = YwRobot Breadboard Power Supply [part_number="VCC -> 5v"]
  R1 = Resistor [tolerance=±5% power=0.25W resistance=10k package=THT]
  IC1 = L293D [package=THT]
  S1 = Pushbutton [package="[THT]"]
  R3 = Resistor [tolerance=±5% power=0.25W resistance=10k package=THT]

nets:
  A15: Part1.A15, MIC.A0
  N1: Part1.SCL, Part2.SCL
  N2: Part1.SDA, Part2.SDA
  GND: Part1.GND, Part2.GND, MIC.G, LCD1.VSS, LCD1.R/W, LCD1.LED-, Power_supply.GND, IC1.0V, R3.Pin_1
  D11: Part1.D11_PWM, LCD1.DB7
  D10: Part1.D10_PWM, LCD1.DB6
  D9: Part1.D9_PWM, LCD1.DB5
  D8: Part1.D8_PWM, LCD1.DB4
  5V: Part1.VIN, Part2.VCC, MIC.+, LCD1.VDD, R2.Pin_0, Power_supply.VCC, IC1.+Vmotor
  D2: Part1.D2_PWM, IC1.In_1
  D3: Part1.D3_PWM, IC1.In_2
  D4: Part1.D4_PWM
  D5: Part1.D5_PWM, LCD1.V0
  D6: Part1.D6_PWM, LCD1.RS
  D7: Part1.D7_PWM, LCD1.E
  D22: Part1.D22, R1.Pin_0
  D33: Part1.D33, MIC.D0
  N3: Part1.D37, S1.Pin_3, S1.Pin_4
  N4: M1.pin_1, IC1.Out_1_(_Controlled_by_Enable_1_)
  N5: M1.pin_2, IC1.Out_2_(_Controlled_by_Enable_1_)
  N6: LCD1.LED+, R2.Pin_1
  N7: R1.Pin_1, IC1.Enable_1
  N8: S1.Pin_1, S1.Pin_2, R3.Pin_0

custom parts:
  Adafruit DS1307 RTC Breakout: This is a great battery-backed real time clock (RTC) that allows your microcontroller project to keep track of time even if it is reprogrammed, or if the power is lost. Perfect for datalogging, clock-building, time stamping, timers and alarms, etc. The DS1307 is the most popular RTC - but it requires 5V power to work (although we've used it with 5V power and 3.3V logic successfully) PCB &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
  KY-037 Sound Sensor Module: Microphone Sound Sensor. It reacts on specific sound volume (Digital Output).
  YwRobot Breadboard Power Supply: The YwRobot Breadboard Power Supply (MB-V2) has two power rails; they can be 5V or 3V3. Power to the module can be provided through the female USB socket or through the A10 (female) 2.1mm power jack.
